# Fritzing sketch ESPClock (saved by Fritzing 0.9.3b)
circuit board: 9.8cm x 3.5cm
breadboards: 1

parts:
  IC1 = Voltage Regulator LM1117 [part_number=AMS1117 package=sot223]
  C5 = Tantalum Capacitor [capacitance=10µF package="A 3216 [SMD, tantalum]"]
  R7 = PHOTOCELL [package=photocell]
  Power_plug1 = Power plug
  UART = male pin header, 4 pins [form="♂ (male)"]
  U2 = MAX7219 [package=dil24]
  R2 = Resistor [tolerance=±5% resistance=10k package="0805 [SMD]"]
  R3 = Resistor [tolerance=±5% resistance=10k package="0805 [SMD]"]
  R9 = Resistor [tolerance=±5% resistance=10k package="0805 [SMD]"]
  R8 = Resistor [tolerance=±5% resistance=10k package="0805 [SMD]"]
  R5 = Resistor [tolerance=±5% resistance=10k package="0805 [SMD]"]
  R4 = Resistor [tolerance=±5% resistance=10k package="0805 [SMD]"]
  R6 = Resistor [tolerance=±5% resistance=10k package="0805 [SMD]"]
  R10 = Resistor [tolerance=±5% resistance=10k package="0805 [SMD]"]
  7_Segment4 = 7 Segment Display
  7_Segment3 = 7 Segment Display
  7_Segment2 = 7 Segment Display
  7_Segment1 = 7 Segment Display
  RESET = Pushbutton [package="[THT]"]
  FLASH = Pushbutton [package="[THT]"]
  C7 = Ceramic Capacitor [capacitance=100nF package="100 mil [THT, multilayer]"]
  DHT12 = DHT11 Humitidy and Temperature Sensor
  U1 = ESP8266 WiFi Module [part_number=ESP8266]
  J1 = Piezo Speaker
  D2 = Diode [package=sma-diode-kit]
  C4 = Tantalum Capacitor [capacitance=10µF package="A 3216 [SMD, tantalum]"]

nets:
  GND: IC1.ADJ, C5.-, R7.P$1, Power_plug1.GND, UART.pin4, U2.GND, U2.GND2, R6.Pin_0, RESET.Pin_2, FLASH.Pin_1, C7.0, DHT12.GND, U1.GND, J1.pin2, C4.-
  +3V3: IC1.OUT, UART.pin1, R2.Pin_0, R3.Pin_0, R9.Pin_0, R8.Pin_1, R5.Pin_0, R4.Pin_0, DHT12.VDD, U1.VCC, C4.+
  VIN: IC1.IN, C5.+, U2.VCC, R10.Pin_1, C7.1, D2.C
  ADC: R7.P$2, R8.Pin_0, U1.ADC_0
  N1: Power_plug1.VCC, D2.A
  TXD: UART.pin2, U1.TXD
  RXD: UART.pin3, U1.RXD
  MOSI: U2.DIN, U1.GPIO_13
  DIG0: U2.DIG0, 7_Segment1.common_anode
  DIG2: U2.DIG2, 7_Segment3.common_anode
  DIG3: U2.DIG3, 7_Segment2.common_anode
  DIG1: U2.DIG1, 7_Segment4.common_anode
  CS: U2.LOAD, U1.GPIO_5
  CLK/GPIO14: U2.CLK, U1.GPIO_14
  SEGA: U2.SEGA, 7_Segment4.Segment_A, 7_Segment3.Segment_A, 7_Segment2.Segment_A, 7_Segment1.Segment_A
  SEGF: U2.SEGF, 7_Segment4.Segment_F, 7_Segment3.Segment_F, 7_Segment2.Segment_F, 7_Segment1.Segment_F
  SEGB: U2.SEGB, 7_Segment4.Segment_B, 7_Segment3.Segment_B, 7_Segment2.Segment_B, 7_Segment1.Segment_B
  SEGG: U2.SEGG, 7_Segment4.Segment_G, 7_Segment3.Segment_G, 7_Segment2.Segment_G, 7_Segment1.Segment_G
  N2: U2.ISET, R10.Pin_0
  SEGC: U2.SEGC, 7_Segment4.Segment_C, 7_Segment3.Segment_C, 7_Segment2.Segment_C, 7_Segment1.Segment_C
  SEGE: U2.SEGE, 7_Segment4.Segment_E, 7_Segment3.Segment_E, 7_Segment2.Segment_E, 7_Segment1.Segment_E
  SEGDP: U2.SEGDP, 7_Segment4.Segment_DP, 7_Segment3.Segment_DP, 7_Segment2.Segment_DP, 7_Segment1.Segment_DP
  SEGD: U2.SEGD, 7_Segment4.Segment_D, 7_Segment3.Segment_D, 7_Segment2.Segment_D, 7_Segment1.Segment_D
  EN: R2.Pin_1, U1.CH_PD
  RST: R3.Pin_1, RESET.Pin_1, U1.REST
  DHT11: R9.Pin_1, DHT12.DATA, U1.GPIO_4
  GPIO0: R5.Pin_1, FLASH.Pin_2, U1.GPIO_0
  GPIO2: R4.Pin_1, U1.GPIO_2
  GPIO15: R6.Pin_1, U1.GPIO_15
  GPIO16: U1.GPIO_16, J1.pin1
  GPIO12: U1.GPIO_12

notes:
  GND
  RX
  TX
  3.3v
  Morgan's ESPClock 2017

custom parts:
  7 Segment Display: 7 Segment Display with common anode.
  Pushbutton: A generic pushbutton.
  DHT11 Humitidy and Temperature Sensor: DHT11 Humidity and Temperature Sensor
  Piezo Speaker: Piezo
